# Fritzing sketch openbot-diy-power-hub (saved by Fritzing 1.0.8)

parts:
  BAT1_·_батарея = 3 × 18650 · 3S
  SW1_·_ON/OFF = SW1 · питание
  Адаптер_L298N_·_3_линии = L298N · три линии питания
  Основная_плата_питания = Плата питания · BAT / SW / L298N / A7 / periferial
  Отдельная_плата_·_распределительная_колодка = Распределительная колодка · отдельная плата
  R1_·_20_кОм = R1
  R2_·_10_кОм = R2
  heading = heading  # not connected
  nano_note = nano_note  # not connected
  footer = footer  # not connected

nets:
  N1: BAT1_·_батарея.+, SW1_·_ON/OFF.IN, SW1_·_ON/OFF.OUT, Адаптер_L298N_·_3_линии.+12V, Основная_плата_питания.BAT+, Основная_плата_питания.SW_IN, Основная_плата_питания.SW_OUT, Основная_плата_питания.VBAT_L298N, Основная_плата_питания.VBAT_R1, R1_·_20_кОм.1
  GND: BAT1_·_батарея.GND, Адаптер_L298N_·_3_линии.GND, Основная_плата_питания.GND_BAT, Основная_плата_питания.GND_L298N, Основная_плата_питания.GND_NANO, Основная_плата_питания.GND_periferial, Основная_плата_питания.GND_R2, Отдельная_плата_·_распределительная_колодка.GND_IN, Отдельная_плата_·_распределительная_колодка.GND_OLED, Отдельная_плата_·_распределительная_колодка.GND_HC-SR04, Отдельная_плата_·_распределительная_колодка.GND_FC-03_L, Отдельная_плата_·_распределительная_колодка.GND_FC-03_R, Отдельная_плата_·_распределительная_колодка.GND_spare, R2_·_10_кОм.2
  N2: Адаптер_L298N_·_3_линии.5V, Основная_плата_питания.5V_L298N, Основная_плата_питания.5V_periferial, Отдельная_плата_·_распределительная_колодка.5V_IN, Отдельная_плата_·_распределительная_колодка.5V_OLED, Отдельная_плата_·_распределительная_колодка.5V_HC-SR04, Отдельная_плата_·_распределительная_колодка.5V_FC-03_L, Отдельная_плата_·_распределительная_колодка.5V_FC-03_R, Отдельная_плата_·_распределительная_колодка.5V_spare
  N3: Основная_плата_питания.A7_NANO, R1_·_20_кОм.2, R2_·_10_кОм.1

custom parts:
  3 × 18650 · 3S: OpenBot DIY: bundled Fritzing library artwork adapted to the existing connector IDs. Original author and license: library-parts/sources.json. See README.breadboard.ru-RU.md. Source: https://forum.fritzing.org/t/18650-battery-holder-part-design/6523/32; Published Fritzing part; no explicit license in FZP
  SW1 · питание: OpenBot DIY: bundled Fritzing library artwork adapted to the existing connector IDs. Original author and license: library-parts/sources.json. See README.breadboard.ru-RU.md. Source: https://github.com/fritzing/fritzing-parts/blob/develop/core/basic-toggle-switch.fzp; CC BY-SA 3.0
  L298N · три линии питания: OpenBot detachable power module wiring. CC BY-SA 3.0. Artwork credits: Fritzing core, Peter Van Epp. Wiring and layout only; no manufacturing PCB view.
  Плата питания · BAT / SW / L298N / A7 / periferial: OpenBot detachable power module wiring. CC BY-SA 3.0. Artwork credits: Fritzing core, Peter Van Epp. Wiring and layout only; no manufacturing PCB view.
  Распределительная колодка · отдельная плата: OpenBot detachable power module wiring. CC BY-SA 3.0. Artwork credits: Fritzing core, Peter Van Epp. Wiring and layout only; no manufacturing PCB view.
  R1: OpenBot DIY: bundled Fritzing library artwork adapted to the existing connector IDs. Original author and license: library-parts/sources.json. See README.breadboard.ru-RU.md. Source: https://github.com/fritzing/fritzing-parts/blob/develop/core/resistor.fzp; CC BY-SA 3.0
  R2: OpenBot DIY: bundled Fritzing library artwork adapted to the existing connector IDs. Original author and license: library-parts/sources.json. See README.breadboard.ru-RU.md. Source: https://github.com/fritzing/fritzing-parts/blob/develop/core/resistor.fzp; CC BY-SA 3.0
  heading: OpenBot detachable power module wiring. CC BY-SA 3.0. Artwork credits: Fritzing core, Peter Van Epp. Wiring and layout only; no manufacturing PCB view.
  nano_note: OpenBot detachable power module wiring. CC BY-SA 3.0. Artwork credits: Fritzing core, Peter Van Epp. Wiring and layout only; no manufacturing PCB view.
  footer: OpenBot detachable power module wiring. CC BY-SA 3.0. Artwork credits: Fritzing core, Peter Van Epp. Wiring and layout only; no manufacturing PCB view.
